# Fritzing sketch wiring2 (saved by Fritzing 0.9.3b)

parts:
  Bauteil3 = Arduino Pro Mini (5V)
  R1 = Resistor [tolerance=±5% resistance=330 package="2010 [SMD]"]
  LED2 = LED - 3mm [color="Red (633nm)" package="3 mm [THT]"]
  S3 = Momentary Switch [package=ksa_sealed_tac_switch]
  JP1 = Header 8 [package=1x08_smd_alt]
  R3 = Resistor [tolerance=±5% resistance=470k package="2010 [SMD]"]
  R4 = Resistor [tolerance=±5% resistance=100k package="2010 [SMD]"]
  VCC1 = 4 x AAA Battery Mount

nets:
  N1: Bauteil3.RAW, R3.Pin_1, VCC1.+
  N2: Bauteil3.GND, LED2.cathode, S3.3, JP1.2, VCC1.-
  N3: Bauteil3.VCC, JP1.1
  N4: Bauteil3.A3, R3.Pin_0, R4.Pin_1
  N5: Bauteil3.SCK, JP1.4
  N6: Bauteil3.MISO, JP1.5
  N7: Bauteil3.MOSI, JP1.3
  N8: Bauteil3.D10, JP1.8
  N9: Bauteil3.D8, S3.1
  N10: Bauteil3.D6, R4.Pin_0
  N11: Bauteil3.D4, R1.Pin_1
  N12: Bauteil3.D2, JP1.7
  N13: R1.Pin_0, LED2.anode
